// Logisim project lecture.circ as structural Verilog: 1 circuit, main circuit main
module main (
  input  A,
  input  B,
  input  Cin,
  input  A_2,
  input  B_2,
  output Sum,
  output out_7,
  output Count,
  output out_9,
  output out_10
);

  wire and_1_out, and_2_out, and_3_out, and_4_out, and_5_out, and_6_out, not_1_out, not_2_out, not_3_out,
       not_4_out, or_2_out, xor_2_out;

  and and_1 (and_1_out, A_2, not_1_out);
  not not_1 (not_1_out, B_2);
  not not_2 (not_2_out, A_2);
  and and_2 (and_2_out, not_2_out, B_2);
  and and_3 (and_3_out, A_2, B_2);
  not not_3 (not_3_out, A_2);
  and and_4 (and_4_out, not_3_out, not_4_out);
  not not_4 (not_4_out, B_2);
  xor xor_1 (out_7, A_2, B_2);
  or or_1 (out_9, and_1_out, and_2_out);
  not not_5 (out_10, or_2_out);
  or or_2 (or_2_out, and_3_out, and_4_out);
  xor xor_2 (xor_2_out, A, B);
  and and_5 (and_5_out, xor_2_out, Cin);
  and and_6 (and_6_out, B, A);
  xor xor_3 (Sum, xor_2_out, Cin);
  or or_3 (Count, and_5_out, and_6_out);
endmodule
